// Digital circuit CPU_With_Registers.dig as structural Verilog
module CPU_With_Registers (
  input  [31:0] n_ins_in_ROM,
  input  Enable,
  input  clk,
  input  in_18,
  input  in_20,
  input  [7:0] O_Value_Constant,
  input  Show_Output,
  input  [7:0] CONSTANT,
  input  in_31,
  input  [7:0] in_33,
  input  in_36,
  input  in_38,
  input  in_40,
  input  in_42,
  input  [7:0] B,
  input  [7:0] _32,
  input  clk_2,
  input  [1:0] Constant_2,
  input  in_50,
  input  [7:0] _17,
  input  [7:0] _28,
  input  [7:0] _12,
  input  [7:0] _42,
  input  in_59,
  input  in_61,
  input  [7:0] O_Value_Constant_2,
  input  in_66,
  input  in_68,
  input  [7:0] O_Value_Constant_3,
  input  [7:0] in_73,
  input  in_74,
  input  clk_3,
  input  in_78,
  output [31:0] Counter_Value,
  output out_2,
  output out_4,
  output is_HALT,
  output [7:0] Data,
  output [4:0] MainOpCode,
  output [7:0] out_10,
  output [7:0] out_11,
  output [7:0] out_12,
  output Last_Bit__Write_Enable_Register_writes_to_itself,
  output Second_Last_Bit__Read_Enable,
  output [7:0] out_15,
  output [7:0] out_16,
  output [7:0] out_17,
  output out_19,
  output out_21,
  output [7:0] out_23,
  output [7:0] out_24,
  output [7:0] out_26,
  output [3:0] out_27,
  output [7:0] Counter_Value_2,
  output out_30,
  output out_32,
  output [7:0] out_34,
  output [7:0] out_35,
  output out_37,
  output out_39,
  output out_41,
  output out_43,
  output [7:0] out_47,
  output [7:0] out_48,
  output out_51,
  output out_52,
  output [7:0] out_57,
  output [7:0] out_58,
  output out_60,
  output out_62,
  output [7:0] out_64,
  output [7:0] out_65,
  output out_67,
  output out_69,
  output [1:0] out_71,
  output out_72,
  output out_75,
  output [7:0] out_77
);

  wire A__eq__B_Flag_q, A__gt__B_flag_q, A__lt__B__Flag_q, and_1_out, and_2_out, and_3_out, and_4_out,
       and_5_out, and_8_out, and_9_out, and_10_out, and_11_out, and_12_out, and_13_out, and_14_out,
       and_15_out, and_17_out, and_18_out, and_19_out, and_20_out, and_21_out, and_22_out, and_23_out,
       and_24_out, and_25_out, and_26_out, and_27_out, and_28_out, and_29_out, and_30_out, and_31_out,
       and_32_out, and_33_out, and_34_out, and_35_out, and_36_out, and_37_out, button_1_out, button_2_out,
       button_3_out, button_4_out, button_5_out, comparator_1_eq, comparator_1_gt, comparator_1_lt,
       decoder_1_out_0, decoder_1_out_1, decoder_1_out_2, decoder_1_out_3, decoder_1_out_4, decoder_1_out_5,
       decoder_1_out_31, decoder_2_out_0, decoder_2_out_1, decoder_2_out_2, decoder_2_out_3, decoder_2_out_4,
       decoder_2_out_5, decoder_2_out_6, decoder_2_out_7, decoder_2_out_8, decoder_2_out_9, decoder_2_out_10,
       decoder_2_out_11, decoder_2_out_12, decoder_3_out_0, decoder_3_out_1, driver_3_out,
       loop_after_certain_value_gt, not_1_out, not_2_out, not_3_out, not_4_out, not_7_out, not_8_out,
       or_1_out, or_2_out, or_4_out, or_5_out, or_6_out, or_8_out, or_9_out;
  wire [3:2] driver_5_out;
  wire [7:0] add_1_s, add_2_s, add_3_s, add_4_s, add_5_s, add_6_s, add_7_s, add_8_s, add_9_s, and_16_out,
       driver_1_out, driver_2_out, driver_6_out, driver_8_out, driver_11_out, driver_15_out, driver_16_out,
       driver_22_out, driver_26_out, multiplexer_1_out, multiplexer_2_out, multiplexer_3_out,
       multiplexer_4_out, not_5_out, not_6_out, or_7_out, sub_1_s, sub_2_s, sub_3_s;
  wire [7:4] driver_5_out_2;

  Register Halt (.D(not_1_out), .C(clk), .en(decoder_1_out_31), .Q(is_HALT));
  not not_1 (not_1_out, is_HALT);
  and and_1 (and_1_out, Enable, not_1_out);
  Button button_1 (.out(button_1_out));
  Button button_2 (.out(button_2_out));
  Button button_3 (.out(button_3_out));
  Button button_4 (.out(button_4_out));
  assign driver_1_out = in_78 ? add_1_s : 8'bz;  // Driver driver_1
  not not_2 (not_2_out, is_HALT);
  Register #(.Bits(8)) A (.D(driver_1_out), .C(clk_3), .en(in_78), .Q(out_77));
  assign driver_2_out = or_1_out ? Data : 8'bz;  // Driver driver_2
  Button button_5 (.out(button_5_out));
  assign driver_3_out = not_2_out ? clk : 1'bz;  // Driver driver_3
  not not_3 (not_3_out, or_1_out);
  Counter #(.Bits(32), .isProgramCounter("true")) Counter (
    .en(and_1_out), .C(driver_3_out), .clr(button_5_out), .out(Counter_Value), .ovf(out_2));
  assign driver_2_out = not_3_out ? add_2_s : 8'bz;  // Driver driver_4
  Comparator #(.Bits(32)) loop_after_certain_value (
    .a(Counter_Value), .b(n_ins_in_ROM), .gt(loop_after_certain_value_gt), .eq(out_30), .lt(out_4));
  or or_1 (or_1_out, or_2_out, decoder_1_out_2);
  Add #(.Bits(8)) add_1 (.a(out_77), .b(in_73), .c_i(in_74), .s(add_1_s), .c_o(out_75));
  Add #(.Bits(8)) add_2 (.a(Counter_Value_2), .b(in_33), .c_i(in_31), .s(add_2_s), .c_o(out_32));
  ROM #(.AddrBits(8), .Bits(8)) A_2 (.A(Counter_Value_2), .sel(not_2_out), .D(Data));
  ROM #(.AddrBits(8), .Bits(5)) ins (.A(Counter_Value_2), .sel(not_2_out), .D(MainOpCode));
  Register #(.Bits(8)) Program_Counter (.D(driver_2_out), .C(driver_3_out), .en(and_1_out), .Q(Counter_Value_2));
  or or_2 (or_2_out, or_4_out, and_2_out);
  or or_3 (out_72, loop_after_certain_value_gt, loop_after_certain_value_gt);
  Decoder #(.Selector_Bits(5)) decoder_1 (
    .sel(MainOpCode), .out_0(decoder_1_out_0), .out_1(decoder_1_out_1), .out_2(decoder_1_out_2),
    .out_3(decoder_1_out_3), .out_4(decoder_1_out_4), .out_5(decoder_1_out_5), .out_31(decoder_1_out_31));  // open: out_6, out_7, out_8, out_9, out_10, out_11, out_12, out_13, out_14, out_15, out_16, out_17, out_18, out_19, out_20, out_21, out_22, out_23, out_24, out_25, out_26, out_27, out_28, out_29, out_30
  or or_4 (or_4_out, and_8_out, and_3_out);
  Register #(.Bits(8)) temp_register (.D(driver_11_out), .C(clk), .en(and_5_out), .Q(out_16));
  assign {driver_5_out_2, driver_5_out, out_71} = not_4_out ? Data : 8'bz;  // Driver driver_5
  not not_4 (not_4_out, and_4_out);
  assign driver_6_out = button_1_out ? _32 : 8'bz;  // Driver driver_6
  and and_2 (and_2_out, A__eq__B_Flag_q, decoder_1_out_5);
  assign driver_6_out = in_50 ? driver_15_out : 8'bz;  // Driver driver_7
  or or_5 (or_5_out, in_50, button_1_out);
  assign driver_8_out = button_3_out ? _32 : 8'bz;  // Driver driver_8
  assign {driver_5_out_2, driver_5_out, out_71} = and_4_out ? out_16 : 8'bz;  // Driver driver_9
  assign driver_8_out = in_50 ? driver_16_out : 8'bz;  // Driver driver_10
  or or_6 (or_6_out, in_50, button_3_out);
  Register #(.Bits(8)) Saved_Register_Operation (.D(Data), .C(clk), .en(decoder_1_out_0), .Q(out_15));
  and and_3 (and_3_out, A__lt__B__Flag_q, decoder_1_out_3);
  Register #(.Bits(8)) A_3 (.D({driver_5_out_2, driver_5_out, out_71}), .C(clk), .en(and_9_out), .Q(out_10));
  and and_4 (and_4_out, out_15[7], Last_Bit__Write_Enable_Register_writes_to_itself);
  and and_5 (and_5_out, out_15[6], Second_Last_Bit__Read_Enable);
  and and_6 (Second_Last_Bit__Read_Enable, out_15[1], decoder_1_out_1);
  and and_7 (Last_Bit__Write_Enable_Register_writes_to_itself, decoder_1_out_1, out_15[0]);
  and and_8 (and_8_out, A__gt__B_flag_q, decoder_1_out_4);
  Register #(.Bits(8)) A1 (.D(driver_6_out), .C(clk_2), .en(or_5_out), .Q(out_34));
  Register #(.Bits(8)) A2 (.D(driver_8_out), .C(clk_2), .en(or_6_out), .Q(out_35));
  assign driver_11_out = and_10_out ? out_10 : 8'bz;  // Driver driver_11
  Register #(.Bits(8)) u_B (.D({driver_5_out_2, driver_5_out, out_71}), .C(clk), .en(and_11_out), .Q(out_11));
  and and_9 (and_9_out, Last_Bit__Write_Enable_Register_writes_to_itself, decoder_2_out_0);
  Add #(.Bits(8)) add_3 (.a(out_10), .b(out_11), .c_i(in_18), .s(add_3_s), .c_o(out_19));
  Sub #(.Bits(8)) sub_1 (.a(out_10), .b(out_11), .c_i(in_20), .s(sub_1_s), .c_o(out_21));
  assign driver_11_out = and_12_out ? out_11 : 8'bz;  // Driver driver_12
  and and_10 (and_10_out, decoder_2_out_0, Second_Last_Bit__Read_Enable);
  Register #(.Bits(8)) C (.D({driver_5_out_2, driver_5_out, out_71}), .C(clk), .en(and_13_out), .Q(out_12));
  and and_11 (and_11_out, Last_Bit__Write_Enable_Register_writes_to_itself, decoder_2_out_1);
  assign driver_11_out = and_14_out ? out_12 : 8'bz;  // Driver driver_13
  and and_12 (and_12_out, decoder_2_out_1, Second_Last_Bit__Read_Enable);
  Register #(.Bits(8)) B1 (.D(B), .C(clk_2), .en(button_2_out), .Q(out_47));
  Register #(.Bits(8)) B2 (.D(B), .C(clk_2), .en(button_4_out), .Q(out_48));
  Decoder #(.Selector_Bits(4)) decoder_2 (
    .sel(out_15[5:2]), .out_0(decoder_2_out_0), .out_1(decoder_2_out_1), .out_2(decoder_2_out_2),
    .out_3(decoder_2_out_3), .out_4(decoder_2_out_4), .out_5(decoder_2_out_5), .out_6(decoder_2_out_6),
    .out_7(decoder_2_out_7), .out_8(decoder_2_out_8), .out_9(decoder_2_out_9), .out_10(decoder_2_out_10),
    .out_11(decoder_2_out_11), .out_12(decoder_2_out_12));  // open: out_13, out_14, out_15
  Register #(.Bits(8)) ALU_ACCUM (.D(multiplexer_1_out), .C(clk), .en(and_19_out), .Q(out_17));
  Multiplexer #(.Selector_Bits(2), .Bits(8)) multiplexer_1 (
    .sel(out_71), .in_0(add_3_s), .in_1(sub_1_s), .in_2(O_Value_Constant), .in_3(O_Value_Constant),
    .out(multiplexer_1_out));
  Add #(.Bits(8)) add_4 (.a(out_34), .b(out_47), .c_i(in_40), .s(add_4_s), .c_o(out_41));
  Sub #(.Bits(8)) sub_2 (.a(out_34), .b(out_47), .c_i(in_42), .s(sub_2_s), .c_o(out_43));
  Add #(.Bits(8)) add_5 (.a(out_35), .b(out_48), .c_i(in_36), .s(add_5_s), .c_o(out_37));
  Sub #(.Bits(8)) sub_3 (.a(out_35), .b(out_48), .c_i(in_38), .s(sub_3_s), .c_o(out_39));
  assign driver_11_out = and_19_out ? multiplexer_1_out : 8'bz;  // Driver driver_14
  and and_13 (and_13_out, Last_Bit__Write_Enable_Register_writes_to_itself, decoder_2_out_2);
  and and_14 (and_14_out, decoder_2_out_2, Second_Last_Bit__Read_Enable);
  and and_15 (and_15_out, in_50, decoder_3_out_0);
  assign and_16_out = out_10 & out_11;  // And and_16, 8 bits wide
  assign or_7_out = out_10 | out_11;  // Or or_7, 8 bits wide
  assign not_5_out = ~out_10;  // Not not_5, 8 bits wide
  assign not_6_out = ~out_11;  // Not not_6, 8 bits wide
  Comparator #(.Bits(8)) comparator_1 (
    .a(out_10), .b(out_11), .gt(comparator_1_gt), .eq(comparator_1_eq), .lt(comparator_1_lt));
  assign driver_15_out = and_15_out ? add_4_s : 8'bz;  // Driver driver_15
  assign driver_16_out = and_17_out ? add_5_s : 8'bz;  // Driver driver_16
  and and_17 (and_17_out, in_50, decoder_3_out_0);
  and and_18 (and_18_out, Last_Bit__Write_Enable_Register_writes_to_itself, decoder_2_out_3);
  Register A__eq__B_Flag (.D(comparator_1_gt), .C(clk), .en(and_24_out), .Q(A__eq__B_Flag_q));
  Register A__gt__B_flag (.D(comparator_1_eq), .C(clk), .en(and_24_out), .Q(A__gt__B_flag_q));
  Register A__lt__B__Flag (.D(comparator_1_lt), .C(clk), .en(and_24_out), .Q(A__lt__B__Flag_q));
  and and_19 (and_19_out, decoder_2_out_3, Second_Last_Bit__Read_Enable);
  assign driver_15_out = and_20_out ? sub_2_s : 8'bz;  // Driver driver_17
  and and_20 (and_20_out, in_50, decoder_3_out_1);
  assign driver_16_out = and_21_out ? sub_3_s : 8'bz;  // Driver driver_18
  and and_21 (and_21_out, in_50, decoder_3_out_1);
  LED led_1 (.in(comparator_1_gt));
  LED led_2 (.in(comparator_1_eq));
  LED led_3 (.in(comparator_1_lt));
  LED led_4 (.in(A__eq__B_Flag_q));
  LED led_5 (.in(A__gt__B_flag_q));
  LED led_6 (.in(A__lt__B__Flag_q));
  Register #(.Bits(8)) LOGIC_ACCUM (.D(multiplexer_2_out), .C(clk), .en(and_23_out), .Q(out_23));
  and and_22 (and_22_out, Last_Bit__Write_Enable_Register_writes_to_itself, decoder_2_out_4);
  Multiplexer #(.Selector_Bits(4), .Bits(8)) multiplexer_2 (
    .sel({driver_5_out, out_71}), .in_0(and_16_out), .in_1(or_7_out), .in_2(not_5_out), .in_3(not_6_out),
    .in_4(CONSTANT), .in_5(CONSTANT), .in_6(CONSTANT), .in_7(CONSTANT), .in_8(CONSTANT), .in_9(CONSTANT),
    .in_10(CONSTANT), .in_11(CONSTANT), .in_12(CONSTANT), .in_13(CONSTANT), .in_14(CONSTANT),
    .in_15(CONSTANT), .out(multiplexer_2_out));
  and and_23 (and_23_out, decoder_2_out_4, Second_Last_Bit__Read_Enable);
  assign driver_11_out = and_23_out ? multiplexer_2_out : 8'bz;  // Driver driver_19
  and and_24 (and_24_out, decoder_2_out_7, Second_Last_Bit__Read_Enable);
  and and_25 (and_25_out, Last_Bit__Write_Enable_Register_writes_to_itself, decoder_2_out_5);
  Decoder #(.Selector_Bits(2)) decoder_3 (
    .sel(Constant_2), .out_0(decoder_3_out_0), .out_1(decoder_3_out_1), .out_2(out_51), .out_3(out_52));
  Register #(.Bits(8)) Memory_Address_Reg (
    .D({driver_5_out_2, driver_5_out, out_71}), .C(clk), .en(and_25_out), .Q(out_24));
  and and_26 (and_26_out, decoder_2_out_5, Second_Last_Bit__Read_Enable);
  assign driver_11_out = and_26_out ? out_24 : 8'bz;  // Driver driver_20
  and and_27 (and_27_out, Last_Bit__Write_Enable_Register_writes_to_itself, decoder_2_out_6);
  RAMDualPort #(.AddrBits(8), .Bits(8)) ramdualport_1 (
    .A(out_24), .Din({driver_5_out_2, driver_5_out, out_71}), .str(and_27_out), .C(clk), .ld(Show_Output),
    .D(out_26));
  and and_28 (and_28_out, decoder_2_out_6, Second_Last_Bit__Read_Enable);
  assign driver_11_out = and_28_out ? out_26 : 8'bz;  // Driver driver_21
  assign driver_22_out = and_31_out ? multiplexer_3_out : 8'bz;  // Driver driver_22
  not not_7 (not_7_out, and_31_out);
  assign driver_22_out = not_7_out ? {driver_5_out_2, driver_5_out, out_71} : 8'bz;  // Driver driver_23
  Register #(.Bits(8)) SIMD_A1 (.D(driver_22_out), .C(clk), .en(or_8_out), .Q(out_57));
  or or_8 (or_8_out, and_29_out, and_31_out);
  and and_29 (and_29_out, Last_Bit__Write_Enable_Register_writes_to_itself, decoder_2_out_8);
  and and_30 (and_30_out, decoder_2_out_8, Second_Last_Bit__Read_Enable);
  assign driver_11_out = and_30_out ? out_57 : 8'bz;  // Driver driver_24
  Add #(.Bits(8)) add_6 (.a(out_57), .b(out_58), .c_i(in_59), .s(add_6_s), .c_o(out_60));
  Add #(.Bits(8)) add_7 (.a(out_57), .b(out_58), .c_i(in_61), .s(add_7_s), .c_o(out_62));
  and and_31 (and_31_out, Last_Bit__Write_Enable_Register_writes_to_itself, decoder_2_out_10);
  Register #(.Bits(8)) SIMD_B1 (.D({driver_5_out_2, driver_5_out, out_71}), .C(clk), .en(and_32_out), .Q(out_58));
  and and_32 (and_32_out, Last_Bit__Write_Enable_Register_writes_to_itself, decoder_2_out_9);
  Multiplexer #(.Selector_Bits(2), .Bits(8)) multiplexer_3 (
    .sel(out_71), .in_0(add_6_s), .in_1(add_7_s), .in_2(O_Value_Constant_2), .in_3(O_Value_Constant_2),
    .out(multiplexer_3_out));
  assign driver_11_out = and_33_out ? out_58 : 8'bz;  // Driver driver_25
  and and_33 (and_33_out, decoder_2_out_9, Second_Last_Bit__Read_Enable);
  assign driver_26_out = and_31_out ? multiplexer_4_out : 8'bz;  // Driver driver_26
  not not_8 (not_8_out, and_31_out);
  assign driver_26_out = not_8_out ? {driver_5_out_2, driver_5_out, out_71} : 8'bz;  // Driver driver_27
  or or_9 (or_9_out, and_31_out, and_34_out);
  and and_34 (and_34_out, Last_Bit__Write_Enable_Register_writes_to_itself, decoder_2_out_11);
  Register #(.Bits(8)) SIMD_A2 (.D(driver_26_out), .C(clk), .en(or_9_out), .Q(out_64));
  and and_35 (and_35_out, decoder_2_out_11, Second_Last_Bit__Read_Enable);
  assign driver_11_out = and_35_out ? out_64 : 8'bz;  // Driver driver_28
  Add #(.Bits(8)) add_8 (.a(out_64), .b(out_65), .c_i(in_66), .s(add_8_s), .c_o(out_67));
  Add #(.Bits(8)) add_9 (.a(out_64), .b(out_65), .c_i(in_68), .s(add_9_s), .c_o(out_69));
  Register #(.Bits(8)) SIMD_B2 (.D({driver_5_out_2, driver_5_out, out_71}), .C(clk), .en(and_36_out), .Q(out_65));
  and and_36 (and_36_out, Last_Bit__Write_Enable_Register_writes_to_itself, decoder_2_out_12);
  Multiplexer #(.Selector_Bits(2), .Bits(8)) multiplexer_4 (
    .sel(out_71), .in_0(add_8_s), .in_1(add_9_s), .in_2(O_Value_Constant_3), .in_3(O_Value_Constant_3),
    .out(multiplexer_4_out));
  assign driver_11_out = and_37_out ? out_65 : 8'bz;  // Driver driver_29
  and and_37 (and_37_out, decoder_2_out_12, Second_Last_Bit__Read_Enable);

  assign out_27 = out_15[5:2];

  // Notes on the sheet:
  //   n_ins_in_ROM: default 243
  //   Enable: default 1
  //   clk: Hz: 20
  //   Show_Output: default 1
  //   in_33: default 1
  //   B: default 1
  //   _32: default 32
  //   clk_2: Hz: 10
  //   _17: default 17
  //   _28: default 28
  //   _12: default 12
  //   _42: default 42
  //   in_73: default 1
  //   clk_3: Hz: 2
  //   If this instruction executed,
  //   stop the machine
  //   Set B1
  //   Set A2
  //   Set B2
  //   Set PC to Data
  //   Set A1
  //   Set Program Counter directly
  //   contents of A_2 (hex, n*v repeats v):
  //   15,0,19,a,15,1,19,14,15,2,19,1e,15,3,19,28,15,4,19,7,15,1,5a,0,81,0,15,3,5a,0,85,
  //   0,15,5,4e,0,99,0,15,0,5a,0,81,0,5,a,15,0,4e,0,99,0,15,1,5a,0,81,0,5,14,15,1,4e,0,
  //   99,0,1,6,5,9,15,1,4e,0,99,0,15,6,19,1,15,1,5a,0,81,0,5,1,15,1,4e,0,99,0,15,2,5a,0,
  //   81,0,5,3,15,2,4e,0,99,0,15,6,5a,0,81,0,15,4,5a,0,85,0,15,6,4e,0,99,0,15,6,5a,0,81,
  //   0,15,3,5a,0,85,0,1e,0,50,1,8,5,1,15,7,52,0,99,0,15,3,5a,0,81,0,15,4,5a,0,85,0,15,
  //   8,52,1,99,0,15,0,5a,0,85,0,1,5,15,9,4e,0,99,0,15,9,5a,0,81,0,15,1,5a,0,85,0,15,a,
  //   4e,0,99,0,15,a,5a,0,81,0,5,1,15,b,4e,0,99,0,15,b,5a,0,81,0,15,2,5a,0,85,0,15,c,4e,
  //   0,99,0,15,c,5a,0,15,d,99
  //   contents of ins (hex, n*v repeats v):
  //   0,1,0,1,0,1,0,1,0,1,0,1,0,1,0,1,0,1,0,1,0,1,0,1,0,1,0,1,0,1,0,1,0,1,0,1,0,1,0,1,0,
  //   1,0,1,0,1,0,1,0,1,0,1,0,1,0,1,0,1,0,1,0,1,0,1,0,1,0,1,0,1,0,1,0,1,0,1,0,1,0,1,0,1,
  //   0,1,0,1,0,1,0,1,0,1,0,1,0,1,0,1,0,1,0,1,0,1,0,1,0,1,0,1,0,1,0,1,0,1,0,1,0,1,0,1,0,
  //   1,0,1,0,1,0,1,0,1,0,1,0,1,0,1,0,1,3,0,1,0,1,0,1,0,1,0,1,0,1,0,1,0,1,0,1,0,1,0,1,0,
  //   1,0,1,0,1,0,1,0,1,0,1,0,1,0,1,0,1,0,1,0,1,0,1,0,1,0,1,0,1,0,1,0,1,0,1,0,1,0,1,0,1,
  //   0,1,0,1,0,1,0,1,0,1,0,1,0,1,0,1,0,1,0,1,0,1,0,1,0,1,0,1,0,1,0,1,0,1,0,1,1e,1e,1f
  //   Inc Operation
  //   Second bit determines if to read 
  //   directly or from register
  //   0 = directly
  //   1 = tmp reg
  //   Sets a register to read 
  //   A Reg-0000
  //   B Reg-0001
  //   Input Line: ------------------->
  //   To select which arithmatic 
  //   operations
  //   result do we need.
  //   Output Line
  //   SIMD Core
  //   <--A
  //   <--B
  //   Arithmatic Unit
  //   Takes A and B as Input
  //   Perfrom w if enabled
  //   Perfrom r if enabled
  //   --->Enable flag
  //   Perform last saved operation
  //   with new value
  //   As of now,use 
  //   only the last 2 bits as
  //   we dont have many
  //   funcs to perform.
  //   Enable tmp reg
  //   use with last second last op only
  //   Write Output -->
  //   Logic Unit
  //   Immediately write the values to output wire.
  //   Its own value will be modified next clock.
  //   Can't be read
  //   This enables all test conditions
  //   Execute SIMD Operation
  //   SIMD Extensions Here
endmodule
